// Logisim project 4X4_MEMORY_READ_WRITE.circ as structural Verilog: 1 circuit, main circuit main
module main (
);

  wire dipswitch_1_p1, dipswitch_2_p1, dipswitch_2_p2, dipswitch_2_p3, dipswitch_2_p4, dipswitch_2_p5,
       dipswitch_2_p6, dipswitch_2_p7, dipswitch_3_p1, dipswitch_3_p2, dipswitch_3_p3, n7404_1_pin2,
       n7404_1_pin4, n7404_1_pin6, n7404_1_pin10, n7404_1_pin12, n7408_1_pin3, n7408_1_pin6, n7408_1_pin8,
       n7408_1_pin11, n7408_2_pin3, n7408_2_pin6, n7408_2_pin8, n7408_2_pin11, n74139_1_pin1, n74139_1_pin4,
       n74139_1_pin5, n74139_1_pin6, n74139_1_pin7, n74139_1_pin16;

  // DipSwitch #(.number(1)) dipswitch_1: pin names not known; wires that end beside it: dipswitch_1_p1
  // DipSwitch dipswitch_2: pin names not known; wires that end beside it: dipswitch_2_p1, dipswitch_2_p2, dipswitch_2_p3, dipswitch_2_p4, dipswitch_2_p5, dipswitch_2_p6, dipswitch_2_p7
  // DipSwitch #(.number(2)) dipswitch_3: pin names not known; wires that end beside it: dipswitch_3_p1, dipswitch_3_p2, dipswitch_3_p3
  _74139 #(.ShowInternalStructure("true"), .VccGndPorts("true")) u_74139_1 (
    .pin1(n74139_1_pin1), .pin2(dipswitch_3_p2), .pin3(dipswitch_3_p3), .pin4(n74139_1_pin4),
    .pin5(n74139_1_pin5), .pin6(n74139_1_pin6), .pin7(n74139_1_pin7), .pin8(n74139_1_pin1),
    .pin16(n74139_1_pin16));  // open: pin15, pin14, pin13, pin12, pin11, pin10, pin9
  _7408 #(.ShowInternalStructure("true"), .VccGndPorts("true")) u_7408_1 (
    .pin1(dipswitch_1_p1), .pin2(dipswitch_2_p4), .pin3(n7408_1_pin3), .pin4(dipswitch_1_p1),
    .pin5(dipswitch_2_p3), .pin6(n7408_1_pin6), .pin7(n74139_1_pin1), .pin14(n74139_1_pin16),
    .pin13(dipswitch_1_p1), .pin12(dipswitch_3_p1), .pin11(n7408_1_pin11), .pin10(dipswitch_1_p1),
    .pin9(dipswitch_2_p7), .pin8(n7408_1_pin8));
  _7404 #(.ShowInternalStructure("true"), .VccGndPorts("true")) u_7404_1 (
    .pin1(n74139_1_pin4), .pin2(n7404_1_pin2), .pin3(n74139_1_pin5), .pin4(n7404_1_pin4),
    .pin5(n74139_1_pin6), .pin6(n7404_1_pin6), .pin7(n74139_1_pin1), .pin14(n74139_1_pin16),
    .pin13(n74139_1_pin7), .pin12(n7404_1_pin12), .pin11(dipswitch_1_p1), .pin10(n7404_1_pin10));  // open: pin9, pin8
  _7408 #(.ShowInternalStructure("true"), .VccGndPorts("true")) u_7408_2 (
    .pin1(dipswitch_1_p1), .pin2(dipswitch_2_p2), .pin3(n7408_2_pin3), .pin4(dipswitch_1_p1),
    .pin5(dipswitch_2_p1), .pin6(n7408_2_pin6), .pin7(n74139_1_pin1), .pin14(n74139_1_pin16),
    .pin13(dipswitch_1_p1), .pin12(dipswitch_2_p6), .pin11(n7408_2_pin11), .pin10(dipswitch_1_p1),
    .pin9(dipswitch_2_p5), .pin8(n7408_2_pin8));
  // also tied to GND on the sheet: n74139_1_pin1
  // also tied to VCC on the sheet: n74139_1_pin16
endmodule
